# Fritzing sketch Elektrisch schema 1.0 (saved by Fritzing 0.9.3b)
circuit board: 8.46667cm x 5.64444cm
breadboards: 1

parts:
  R1 = Resistor [tolerance=±5% resistance=6.8k package=THT]
  Q1 = NPN-Transistor [part_number=BC547 package="TO92 [THT]"]
  M1 = DC Motor [part_number=Pump]
  Q2 = NPN-Transistor [part_number=BC547 package="TO92 [THT]"]
  R2 = Resistor [tolerance=±5% resistance=6.8k package=THT]
  V1 = Solenoid [part_number=Valve]
  U1 = RELAY [part_number=Relais package=relay-jzc]
  CD1 = Solenoid
  U2 = RELAY [part_number=Relais package=relay-jzc]
  CD2 = Solenoid
  U3 = RELAY [part_number=Relais package=relay-jzc]
  CD3 = Solenoid
  U4 = RELAY [part_number=Relais package=relay-jzc]
  CD4 = Solenoid
  U5 = RELAY [part_number=Relais package=relay-jzc]
  CD5 = Solenoid

nets:
  Pump pin: R1.Pin_0
  N1: R1.Pin_1, Q1.B
  GND: Q1.E, Q2.E, U1.COIL2, U2.COIL2, U3.COIL2, U4.COIL2, U5.COIL2
  N2: Q1.C, M1.pin_2
  12V: M1.pin_1, V1.pin1
  N3: Q2.B, R2.Pin_1
  N4: Q2.C, V1.pin2
  Valve pin: R2.Pin_0
  N5: U1.NO, CD1.pin1
  N6: U1.MAIN, CD1.pin2
  CD1 pin: U1.COIL1
  N7: U2.NO, CD2.pin1
  N8: U2.MAIN, CD2.pin2
  CD2 pin: U2.COIL1
  N9: U3.NO, CD3.pin1
  N10: U3.MAIN, CD3.pin2
  CD3 pin: U3.COIL1
  N11: U4.NO, CD4.pin1
  N12: U4.MAIN, CD4.pin2
  CD4 pin: U4.COIL1
  N13: U5.NO, CD5.pin1
  N14: U5.MAIN, CD5.pin2
  CD5 pin: U5.COIL1
